// Logisim project IC4793.circ as structural Verilog: 1 circuit, main circuit main
module main (
);

  wire j_k_ff_1_q, j_k_ff_2_q, j_k_ff_3_q, j_k_ff_4_q, nand_1_out, undriven, undriven_2;

  // NAND_Gate nand_1 has open pins: out=nand_1_out
  J_K_Flip_Flop j_k_ff_1 (.clk(undriven), .Q(j_k_ff_1_q), .reset(nand_1_out));  // open: J, K, Qn, preset, en
  J_K_Flip_Flop #(.trigger("falling")) j_k_ff_2 (
    .clk(undriven_2), .K(undriven_2), .Q(j_k_ff_2_q), .reset(nand_1_out));  // open: J, Qn, preset, en
  J_K_Flip_Flop #(.trigger("falling")) j_k_ff_3 (
    .Q(j_k_ff_3_q), .reset(nand_1_out));  // open: J, clk, K, Qn, preset, en
  J_K_Flip_Flop #(.trigger("falling")) j_k_ff_4 (
    .Q(j_k_ff_4_q), .en(nand_1_out), .reset(nand_1_out));  // open: J, clk, K, Qn, preset

  // Notes on the sheet:
  //   MR1
  //   CP0
  //   MR2
  //   CP1
  //   Q0
  //   Q1
  //   Q2
  //   3
  //   Q3
endmodule
